# Fritzing sketch relayShield (saved by Fritzing 0.8.7b)
circuit board: 6.9215cm x 5.33756cm
breadboards: 1

parts:
  part = Diode [package=diode-1n4001]  # not connected
  Parte1 = Arduino Uno (Rev3)
  J1 = screw terminal, 2 pins
  R1 = Resistor [tolerance=±5% resistance=1k package=THT]
  Q1 = NPN-Transistor [part_number=2N2222 package="TO92 [THT]"]
  D1 = Diode [part_number=1N4004 package=diode-1n4001]
  U1 = RELAY [package=relay-g5v]
  J2 = screw terminal, 2 pins

nets:
  N1: Parte1.D2, R1.Pin_1
  N2: Parte1.5V, D1.A, U1.5
  N3: Parte1.GND, Q1.E
  N4: J1.pin1, U1.1, J2.pin1
  N5: J1.pin2, U1.3
  N6: R1.Pin_0, Q1.B
  N7: Q1.C, D1.C, U1.2
  N8: U1.4, J2.pin2

notes:
  Plataforma
  Club de
  Electronica

custom parts:
  RELAY: HJR-3FF
